# Fritzing sketch joystick (saved by Fritzing 0.9.2b)
stripboards: 1

parts:
  U1 = mystery part, 5 pins [chip_label=JOYSTICK]
  J1 = Generic shrouded header - 10 pins [form="♂ (shrouded male)" package=THT]
  TRRS1 = Audio Jack (TRRS) 3.5mm [part_number="X OUT" package="RC-5325A [SMD]"]
  TRRS2 = Audio Jack (TRRS) 3.5mm [part_number="Y OUT" package="RC-5325A [SMD]"]
  R1 = Resistor [tolerance=±5% resistance=1k package="2512 [SMD]"]
  R2 = Resistor [tolerance=±5% resistance=1k package="2512 [SMD]"]
  IC1 = Voltage Regulator [package=to-92]

nets:
  GND: U1.pin1, J1.GND, TRRS1.SLEEVE, TRRS2.SLEEVE, IC1.GND
  N1: U1.pin2, IC1.OUT
  N2: U1.pin3, R1.Pin_1
  N3: U1.pin4, R2.Pin_1
  N4: J1.+12V, IC1.IN
  N5: TRRS1.TIP, R1.Pin_0
  N6: TRRS2.TIP, R2.Pin_0

custom parts:
  Generic shrouded header - 10 pins: Generic shrouded header
