# Fritzing sketch r1 (saved by Fritzing 0.9.2b)
stripboards: 1

parts:
  U1 = atmega328 [package=dip]
  JP1 = Header 5x2 [package=2x5-ra]
  U3 = Voltage Regulator - 5V [package="TO220 [THT]"]
  U4 = mystery part, 4 pins [chip_label=GT]
  U5 = mystery part, 4 pins [chip_label=1]
  U6 = mystery part, 4 pins [chip_label=2]
  U7 = mystery part, 4 pins [chip_label=3]
  U8 = mystery part, 4 pins [chip_label=4]
  J1 = shrouded pin header, 6 pins [form="♂ (shrouded male)"]
  LED1 = LED - 5mm [color="Green (560nm)" package="5 mm [THT]"]
  LED2 = LED - 5mm [color="Red (633nm)" package="5 mm [THT]"]
  LED3 = LED - 5mm [color="Red (633nm)" package="5 mm [THT]"]
  LED4 = LED - 5mm [color="Red (633nm)" package="5 mm [THT]"]
  LED5 = LED - 5mm [color="Red (633nm)" package="5 mm [THT]"]
  S1 = Pushbutton [package="[THT]"]
  S2 = Toggle Switch [package=THT]
  R9 = Resistor [tolerance=±5% resistance=1k package=THT]
  R8 = Resistor [tolerance=±5% resistance=1k package=THT]
  R7 = Resistor [tolerance=±5% resistance=1k package=THT]
  R10 = Resistor [tolerance=±5% resistance=1k package=THT]
  R11 = Resistor [tolerance=±5% resistance=1k package=THT]
  R3 = Resistor [tolerance=±5% resistance=220 package=THT]
  R4 = Resistor [tolerance=±5% resistance=220 package=THT]
  R5 = Resistor [tolerance=±5% resistance=220 package=THT]
  R6 = Resistor [tolerance=±5% resistance=220 package=THT]
  R1 = Resistor [tolerance=±5% resistance=10k package=THT]
  D1 = Rectifier Diode [part_number=1N4148 package="300 mil [THT]"]
  R12 = Resistor [tolerance=±5% resistance=10k package=THT]

nets:
  N1: U1.RESET, J1.pin6
  N2: U1.D0_(RX), R11.Pin_0
  N3: U1.D1_(TX), R10.Pin_0
  N4: U1.D2, D1.cathode
  N5: U1.D3_(PWM), S1.Pin_1, R12.Pin_1
  N6: U1.VCC, U3.output_voltage, J1.pin3, S1.Pin_3, S1.Pin_4
  GND: U1.GND, JP1.3, JP1.5, JP1.7, U3.GND, U4.pin2, U4.pin3, U5.pin2, U5.pin3, U6.pin2, U6.pin3, U7.pin2, U7.pin3, U8.pin2, U8.pin3, J1.pin1, LED1.cathode, LED2.cathode, LED3.cathode, LED4.cathode, LED5.cathode, S2.COM, R1.Pin_1, R12.Pin_0
  N7: U1.D5_(PWM), S2.L1
  N8: U1.D6_(PWM), S2.L2
  N9: U1.D7, R6.Pin_0
  N10: U1.D8, R5.Pin_0
  N11: U1.D9_(PWM), R4.Pin_0
  N12: U1.D10_(PWM), R3.Pin_0
  N13: U1.D11_(PWM), J1.pin2, R7.Pin_1
  N14: U1.D12, J1.pin4, R8.Pin_1
  N15: U1.D13, J1.pin5, R9.Pin_1
  N16: JP1.4, JP1.6, JP1.8
  N17: JP1.10, U3.input_voltage
  N18: U4.pin1, U4.pin4, R1.Pin_0, D1.anode
  N19: U5.pin1, U5.pin4, R3.Pin_1
  N20: U6.pin1, U6.pin4, R4.Pin_1
  N21: U7.pin1, U7.pin4, R5.Pin_1
  N22: U8.pin1, U8.pin4, R6.Pin_1
  N23: LED1.anode, R7.Pin_0
  N24: LED2.anode, R8.Pin_0
  N25: LED3.anode, R9.Pin_0
  N26: LED4.anode, R11.Pin_1
  N27: LED5.anode, R10.Pin_1
